# Fritzing sketch wiring-diagram (saved by Fritzing 0.9.2b)
breadboards: 1

parts:
  Parte1 = Motor Driver 1A Dual TB6612FNG  # not connected
  Parte2 = Motor Driver 1A Dual TB6612FNG  # not connected
  14_6V_Battery_(to_7_2V) = LM2596 step down module
  Parte3 = Arduino Mega 2560 (Rev3)
  TBS_Mini = damikro tbs mini
  Parte4 = Motor Driver 1A Dual TB6612FNG  # not connected
  Speaker = SPEAKER [package=pcb_mount_speaker]
  M2 = ps2 gamepad [package=THT]
  Gun_recoil = Basic Servo
  Gun_elevation = Basic Servo
  right_motor = Screw terminal - 2 pins [package=THT]  # not connected
  left_motor = Screw terminal - 2 pins [package=THT]  # not connected
  smoke_generator = Screw terminal - 2 pins [package=THT]  # not connected
  smoke_fan = Screw terminal - 2 pins [package=THT]  # not connected
  turret_rotation = Screw terminal - 2 pins [package=THT]  # not connected

nets:
  GND: 14_6V_Battery_(to_7_2V).IN-, 14_6V_Battery_(to_7_2V).OUT-, Parte3.GND, TBS_Mini.SP-GND, TBS_Mini.Prop1_input_gnd, TBS_Mini.Out_3+4_gnd, TBS_Mini.Prog_GND, Speaker.+, M2.GND, Gun_recoil.gnd, Gun_elevation.gnd
  N1: 14_6V_Battery_(to_7_2V).OUT+, TBS_Mini.Prop1_input_pwr, TBS_Mini.Out_1+2_pwr
  N2: Parte3.A0, M2.ATT
  N3: Parte3.A1, M2.CMD
  N4: Parte3.A2, M2.DAT
  N5: Parte3.A3, M2.CLK
  3V3: Parte3.3V3, M2.3.3V, M2.SHLD
  VCC: Parte3.5V, Gun_recoil.vcc, Gun_elevation.vcc
  N6: Parte3.D37, TBS_Mini.Prop1_input_sig
  N7: Parte3.D39, TBS_Mini.Prop2_input_sig
  N8: Parte3.D41, TBS_Mini.Prop3_input_sig
  N9: Parte3.D43, Gun_recoil.pulse
  N10: Parte3.D45, Gun_elevation.pulse
  N11: TBS_Mini.SP-, Speaker.-

notes:
  turret rotation
  smoke fan
  smoke generator
  left motor
  right motor

custom parts:
  LM2596 step down module: LM2596 DC-DC step down power supply module 3 A.
  damikro tbs mini: damikro tbs mini digital multifunctional RC sound unit. Pcb view has been omitted as not useful.
  ps2 gamepad: PS2 gamepad. Warning! PCB view is designed for the female connector available from https://www.robotshop.com/en/ps2-connector.html. However there is no mechanical information that I can find so ipcb was generated from a scaled jpg and may well be wrong. Print the footprint out and check it against a real part before ordering boards!
